# Fritzing sketch ResQ PCB  (saved by Fritzing 0.9.3b)
breadboards: 1

parts:
  WeMos_D1_Mini1 = WeMos D1 Mini
  OLED = female pin header, 6 pins [form="♀ (female)"]  # not connected
  GPS = female pin header, 6 pins [form="♀ (female)"]  # not connected
  SD_Card = female pin header, 6 pins [form="♀ (female)"]  # not connected
  S1 = SPST Switch [package=switch-spdt]
  VCC = Battery

nets:
  N1: WeMos_D1_Mini1.5V, S1.O
  GND: WeMos_D1_Mini1.G, VCC.+
  N2: S1.P, VCC.-
