# Fritzing sketch ResQ PCB V1.1 Routing  (saved by Fritzing 0.9.3b)
breadboards: 1

parts:
  WeMos_D1_Mini1 = WeMos D1 Mini
  SD_Card = female pin header, 6 pins [form="♀ (female)"]
  S1 = SPST Switch [package=switch-spdt]
  GPS = female pin header, 4 pins [form="♀ (female)"]
  OLED = female pin header, 4 pins [form="♀ (female)"]
  E1 = female pin header, 3 pins [form="♀ (female)"]  # not connected
  E2 = female pin header, 3 pins [form="♀ (female)"]  # not connected
  Vin = female pin header, 2 pins [form="♀ (female)"]

nets:
  N1: WeMos_D1_Mini1.3V3, SD_Card.pin1, GPS.pin4
  N2: WeMos_D1_Mini1.5V, S1.O, OLED.pin1
  N3: WeMos_D1_Mini1.D1, OLED.pin3
  N4: WeMos_D1_Mini1.D2, OLED.pin4
  N5: WeMos_D1_Mini1.D3, GPS.pin3
  N6: WeMos_D1_Mini1.D4, GPS.pin2
  CLK: WeMos_D1_Mini1.D5, SD_Card.pin4
  MISO: WeMos_D1_Mini1.D6, SD_Card.pin5
  MOSI: WeMos_D1_Mini1.D7, SD_Card.pin3
  CS: WeMos_D1_Mini1.D8, SD_Card.pin2
  GND: WeMos_D1_Mini1.G, SD_Card.pin6, OLED.pin2, Vin.pin2
  5V: S1.P, Vin.pin1

notes:
  ResQ Search and Rescue Tool, 1.1
